# Fritzing sketch Cooling Fan Controller (saved by Fritzing 1.0.4)
stripboards: 1

parts:
  IC1 = Voltage Regulator [package=78xxl]
  DS1 = DS18B20 1-Wire Temperature Sensor [part_number=DS18B20]
  R1 = Resistor [tolerance=±5% resistance=220 package="0603 [SMD]"]
  J1 = Camdenboss CTB0158-2 [part_number=CTB0158-2 package=THT]
  D1 = Diode [package=diode-1n4001]
  R2 = Resistor [tolerance=±5% resistance=10k package="0603 [SMD]"]
  M2 = DC Motor [voltage_(max)=12V voltage_(min)=3V]
  DHT11 = DHT11 Humitidy and Temperature Sensor (3 pins)
  R4 = Resistor [tolerance=±5% resistance=10k package="0603 [SMD]"]
  J4 = Camdenboss CTB0158-2 [part_number=CTB0158-2 package=THT]
  V_Battery = DC Power [voltage=12V internal_resistance=0.1Ω]
  Q1 = Basic FET N-Channel [part_number=IRLZ34N package="TO220 [THT]"]
  J2 = Camdenboss CTB0158-2 [part_number=CTB0158-2 package=THT]
  M1 = DC Motor [voltage_(max)=12V voltage_(min)=3V]
  WeMos_D1_Mini1 = WeMos D1 Mini
  J3 = Camdenboss CTB0158-3 [part_number=CTB0158-3 package=THT]
  R3 = Resistor [tolerance=±5% resistance=10k package="0603 [SMD]"]

nets:
  GND: IC1.GND, R2.Pin_0, DHT11.Gnd, J4.pin1, Q1.source, WeMos_D1_Mini1.G, J3.pin1
  12V: IC1.IN, J1.pin1, D1.C, J4.pin2, J2.pin1
  5V: IC1.OUT, DHT11.Plus, R4.Pin_1, WeMos_D1_Mini1.5V, J3.pin3, R3.Pin_1
  N1: DS1.GND, J3.terminal_1
  N2: DS1.DQ, J3.terminal_2
  N3: DS1.VDD, J3.terminal_3
  N4: R1.Pin_0, R2.Pin_1, Q1.gate
  Fan Speed: R1.Pin_1, WeMos_D1_Mini1.D2
  N5: J1.pin2, D1.A, Q1.drain, J2.pin2
  N6: J1.terminal_1, M1.pin_1
  N7: J1.terminal_2, M1.pin_2
  N8: M2.pin_1, J2.terminal_1
  N9: M2.pin_2, J2.terminal_2
  Ambient Temperature: DHT11.Signal, R4.Pin_0, WeMos_D1_Mini1.D5
  N10: J4.terminal_1, V_Battery.V+
  N11: J4.terminal_2, V_Battery.V-
  Charger Temperature: WeMos_D1_Mini1.D7, J3.pin2, R3.Pin_0

notes:
  12V to 5V Buck Converter
  Ambient Temperature Sensor
  Charger Temperature Sensor
  Fan Speed Driver
  The Brain

custom parts:
  DHT11 Humitidy and Temperature Sensor (3 pins): DHT11 Humidity and Temperature Sensor (3 pins).
